# Fritzing sketch schema_proiect (saved by Fritzing 0.9.9b)
circuit board: 21.1726cm x 10.6878cm
breadboards: 1

parts:
  Part1 = TFT 2.8 inch 320x240 Touch w microSD [part_number=1770]
  Part2 = Thumb Joystick
  R1 = Resistor [tolerance=±5% resistance=220 package="2010 [SMD]"]
  Part3 = Arduino Uno (Rev3) - ICSP
  Part4 = Thumb Joystick
  R2 = Resistor [tolerance=±5% resistance=220 package="2010 [SMD]"]
  R4 = Resistor [tolerance=±5% resistance=220 package="2010 [SMD]"]
  J1 = Piezo Speaker
  J2 = Piezo Speaker
  R5 = Resistor [tolerance=±5% resistance=220 package="2010 [SMD]"]
  R3 = Resistor [tolerance=±5% resistance=220 package="2010 [SMD]"]

nets:
  GND: Part1.GND, Part2.GND, Part3.GND, Part4.GND, J1.pin1, J2.pin1
  VCC: Part1.+5V, Part1.LCD_CS, Part2.VCC, Part3.5V, Part4.VCC, R3.Pin_0
  N1: Part1.LCD_DC, R4.Pin_0
  N2: Part1.LCD_RST, R5.Pin_0
  N3: Part1.SCLK, R1.Pin_0
  N4: Part1.MISO, Part3.D12/MISO
  N5: Part1.MOSI, R2.Pin_0
  N6: Part2.HORZ, Part3.A2
  N7: Part2.VERT, Part3.A3
  N8: R1.Pin_1, Part3.ICSP_SCK, Part3.D13/SCK
  N9: Part3.A0, Part4.HORZ
  N10: Part3.A1, Part4.VERT
  N11: Part3.ICSP_MOSI, Part3.D11_PWM/MOSI, R2.Pin_1
  N12: Part3.D8, R3.Pin_1
  N13: Part3.D9_PWM, R4.Pin_1
  N14: Part3.D10_PWM/SS, R5.Pin_1
  N15: Part3.D5_PWM, J2.pin2
  N16: Part3.D6_PWM, J1.pin2

custom parts:
  TFT 2.8 inch 320x240 Touch w microSD: This TFT display is big (2.8" diagonal) bright (4 white-LED backlight) and colorful! 240x320 pixels with individual RGB pixel control. As a bonus, this display has a resistive touchscreen attached to it already, so you can detect finger presses anywhere on the screen.
